# Fritzing sketch word clock schematic (saved by Fritzing 0.9.3b)
breadboards: 1

parts:
  Power_plug1 = Power plug
  R1 = Resistor [tolerance=±5% resistance=470 package=THT]
  C1 = Electrolytic Capacitor [capacitance=1mF package="100 mil [THT, electrolytic]"]
  WS2812b = Dagu DGServo 9g header (male) [package=THT]
  Arduino_micro = Arduino Micro (Rev3)
  DCF77 = IC, SIP package, 4 pins [chip_label=DCF77]
  R2 = Resistor [tolerance=±5% resistance=10k package=THT]

nets:
  GND: Power_plug1.GND, C1.-, WS2812b.gnd, Arduino_micro.GND, DCF77.pin1
  VCC: Power_plug1.VCC, C1.+, WS2812b.Vcc, Arduino_micro.VIN, DCF77.pin2, R2.Pin_0
  N1: R1.Pin_0, Arduino_micro.D9_PWM/A9
  N2: R1.Pin_1, WS2812b.pulse
  N3: Arduino_micro.A5, DCF77.pin3, R2.Pin_1
