# Fritzing sketch DS3231-DCF77 schematic (saved by Fritzing 0.9.3b)
breadboards: 1

parts:
  Arduino_Nano = Arduino Nano (Rev3.0)
  Power_plug1 = Power plug
  R1 = Resistor [tolerance=±5% resistance=470 package=THT]
  C1 = Electrolytic Capacitor [capacitance=1mF package="100 mil [THT, electrolytic]"]
  WS2812b = Dagu DGServo 9g header (male) [package=THT]
  ZS-042_RTC1 = ZS-042 RTC Module
  DCF77 = IC, SIP package, 5 pins [chip_label=DCF77]

nets:
  GND: Arduino_Nano.GND, Power_plug1.GND, WS2812b.gnd, ZS-042_RTC1.GND, DCF77.pin4
  N1: Arduino_Nano.D2, DCF77.pin2
  N2: Arduino_Nano.D7, DCF77.pin1
  N3: Arduino_Nano.D9, R1.Pin_0
  VCC: Arduino_Nano.VIN, Power_plug1.VCC, C1.+, WS2812b.Vcc
  5V: Arduino_Nano.5V, ZS-042_RTC1.VCC
  N4: Arduino_Nano.A5, ZS-042_RTC1.SCL
  N5: Arduino_Nano.A4, ZS-042_RTC1.SDA
  N6: Arduino_Nano.3V3, DCF77.pin5
  N7: R1.Pin_1, WS2812b.pulse
