# Fritzing sketch word clock schematic (saved by Fritzing 0.9.3b)
breadboards: 1

parts:
  Arduino_Nano = Arduino Nano (Rev3.0)
  IC1 = DS1302 [package="DIP8 [THT]"]
  S1 = Pushbutton [package="[THT]"]
  S2 = Pushbutton [package="[THT]"]
  Power_plug1 = Power plug
  R1 = Resistor [tolerance=±5% resistance=470 package=THT]
  C1 = Electrolytic Capacitor [capacitance=1mF package="100 mil [THT, electrolytic]"]
  WS2812b = Dagu DGServo 9g header (male) [package=THT]

nets:
  GND: Arduino_Nano.GND, IC1.0V, S1.Pin_1, S1.Pin_2, S2.Pin_1, S2.Pin_2, Power_plug1.GND, WS2812b.gnd
  N1: Arduino_Nano.D5, IC1.CE_-_Chip_Enable
  N2: Arduino_Nano.D6, IC1.I/O_-_SPI_Data_In/Out
  N3: Arduino_Nano.D7, IC1.SCLK_-_SPI_Clock
  N4: Arduino_Nano.D9, R1.Pin_0
  N5: Arduino_Nano.D10, S2.Pin_3, S2.Pin_4
  N6: Arduino_Nano.D11/MOSI, S1.Pin_3, S1.Pin_4
  VCC: Arduino_Nano.VIN, Power_plug1.VCC, C1.+, WS2812b.Vcc
  N7: Arduino_Nano.5V, IC1.+V
  N8: R1.Pin_1, WS2812b.pulse
